# Fritzing sketch Final_Project_Fritz_IoT_Fall_2025 (saved by Fritzing 1.0.3b)
breadboards: 1

parts:
  LED1 = LED - 5mm [color="Blue (430nm)" current=0.030A package="5 mm [THT]"]
  R1 = Resistor [tolerance=±5% power=0.25W resistance=220 package=THT]  # not connected
  Part1 = Arduino Uno (Rev3)
  J1 = Piezo Speaker
  R2 = Resistor [tolerance=±5% power=0.25W resistance=100 package=THT]
  Part2 = Bluetooth HC-05 Macho  # not connected

nets:
  N1: LED1.cathode, Part1.D8
  N2: Part1.D10_PWM/SS, R2.Pin_1
  N3: J1.pin2, R2.Pin_0
